// Logisim project Data_Memory_and_Jump.circ as structural Verilog: 5 circuits, main circuit main
module main (
  input  Rst,
  input  Clk,
  output [7:0] R0,
  output [7:0] R1,
  output [7:0] R2,
  output [7:0] R3
);

  wire C, cu_1_sub, O, S, Z;
  wire [1:0] cu_1_dest;
  wire [2:0] cu_1_source;
  wire [4:0] PC_q;
  wire [7:0] EPROM_data, IR;

  Counter #(.max('h1f), .width(5)) PC (
    .clr(Rst), .load(1'b0), .up(1'b1), .count(1'b1), .clk(Clk), .D({5{1'b0}}), .Q(PC_q));  // open: carry
  CU cu_1 (
    .IR(IR), .C(C), .Z(Z), .S(S), .O(O), .Source(cu_1_source), .Dest(cu_1_dest), .Sub(cu_1_sub));  // open: En_Read, En_PC, En_Write, Load_SR, OE
  ROM #(.addrWidth(5)) EPROM (.addr(PC_q), .data(EPROM_data));
  Register register_1 (.D(EPROM_data), .en(1'b1), .clk(Clk), .Q(IR), .clr(Rst));
  // DP dp_1: pin names not known; wires that end beside it: cu_1_source, cu_1_dest, cu_1_sub, Clk, Rst, R0, R1, R2, R3, C, Z, S, O, O

  // Notes on the sheet:
  //   contents of EPROM (hex, n*v repeats v):
  //   20 d 1 8 1 8 1 8 1 8 22*4
endmodule

module ALU (
  input  [7:0] A,
  input  [7:0] B,
  input  Op,
  output [7:0] Result,
  output C,
  output Z,
  output S,
  output O
);

  wire adder_1_cout, subtractor_1_bout;
  wire [7:0] adder_1_out, subtractor_1_out;

  Adder adder_1 (.a(A), .b(B), .out(adder_1_out), .cout(adder_1_cout));  // open: cin
  Subtractor subtractor_1 (.a(A), .b(B), .out(subtractor_1_out), .bout(subtractor_1_bout));  // open: bin
  Multiplexer #(.width(8)) multiplexer_1 (.in0(adder_1_out), .in1(subtractor_1_out), .out(Result), .sel(Op));
  Multiplexer multiplexer_2 (.in0(adder_1_cout), .in1(subtractor_1_bout), .out(C), .sel(Op));
  nor nor_1 (Z, Result[0], Result[1], Result[2], Result[3], Result[4], Result[5], Result[6], Result[7]);

  assign S = Result[7];
endmodule

module Reg_File (
  input  Clk,
  input  [1:0] Dest,
  input  [7:0] Data_in,
  input  Rst,
  output [7:0] R0,
  output [7:0] R1,
  output [7:0] R2,
  output [7:0] R3
);

  wire decoder_1_out0, decoder_1_out1, decoder_1_out2, decoder_1_out3;

  Decoder #(.select(2)) decoder_1 (
    .out0(decoder_1_out0), .out1(decoder_1_out1), .out2(decoder_1_out2), .out3(decoder_1_out3), .sel(Dest));  // open: en
  Register register_1 (.D(Data_in), .en(decoder_1_out0), .clk(Clk), .Q(R0), .clr(Rst));
  Register register_2 (.D(Data_in), .en(decoder_1_out1), .clk(Clk), .Q(R1), .clr(Rst));
  Register register_3 (.D(Data_in), .en(decoder_1_out2), .clk(Clk), .Q(R2), .clr(Rst));
  Register register_4 (.D(Data_in), .en(decoder_1_out3), .clk(Clk), .Q(R3), .clr(Rst));
endmodule

module DP (
  input  [2:0] Source,
  input  [1:0] Dest,
  input  Op,
  input  [7:0] Data_In,
  input  Load_SR,
  input  Clk,
  input  Rst,
  output [7:0] ALU_Out,
  output [7:0] R0,
  output [7:0] R1,
  output [7:0] R2,
  output [7:0] R3,
  output C,
  output Z,
  output S,
  output O
);

  wire [3:0] alu_1_c;
  wire [7:0] A, B;

  Reg_File reg_file_1 (.Clk(Clk), .Dest(Dest), .Data_in(Data_In), .Rst(Rst), .R0(R0), .R1(R1), .R2(R2), .R3(R3));
  Multiplexer #(.select(3), .width(8)) multiplexer_1 (
    .in0(R0), .in1(R1), .in2(R2), .in3(R3), .in4({8{1'b0}}), .in5(8'h1), .in6({8{1'b1}}), .out(B),
    .sel(Source));  // open: in7
  ALU alu_1 (.A(A), .B(B), .Op(Op), .Result(ALU_Out), .C(alu_1_c[0]), .Z(alu_1_c[1]), .S(alu_1_c[2]), .O(alu_1_c[3]));
  Multiplexer #(.select(2), .width(8)) multiplexer_2 (.in0(R0), .in1(R1), .in2(R2), .in3(R3), .out(A), .sel(Dest));
  Register #(.width(4)) register_1 (.D(alu_1_c), .en(Load_SR), .clk(Clk), .Q({O, S, Z, C}), .clr(Rst));
endmodule

module CU (
  input  [7:0] IR,
  input  C,
  input  Z,
  input  S,
  input  O,
  output [2:0] Source,
  output [1:0] Dest,
  output En_Read,
  output En_PC,
  output En_Write,
  output Sub,
  output Load_SR,
  output OE
);

  wire Mem_Inst, multiplexer_1_out, not_1_out, not_2_out, not_3_out, not_4_out;

  Multiplexer #(.select(2)) multiplexer_1 (
    .in0(Z), .in1(S), .in2(O), .in3(1'b1), .out(multiplexer_1_out), .sel(IR[6:5]));
  and and_1 (En_PC, multiplexer_1_out, IR[7]);
  and and_2 (Mem_Inst, IR[6], not_1_out);
  not not_1 (not_1_out, IR[7]);
  not not_2 (not_2_out, IR[6]);
  and and_3 (Load_SR, not_2_out, not_3_out);
  not not_3 (not_3_out, IR[7]);
  and and_4 (En_Write, Mem_Inst, IR[5]);
  and and_5 (En_Read, Mem_Inst, not_4_out);
  not not_4 (not_4_out, IR[5]);

  assign Dest = IR[4:3];
  assign OE = Load_SR;
  assign Source = IR[2:0];
  assign Sub = IR[5];

  // Other names for the same wires on the sheet: ALU_Inst = Load_SR; Branch_Address[4:0] = IR[4:0];
  //   Mem_Address[4:0] = IR[4:0]; J_Condition[1:0] = IR[6:5]; Write = IR[5]; Opcode[1:0] = IR[7:6]; Jump_Inst = IR[7]
endmodule
